# Fritzing sketch esp-fish-feeder (saved by Fritzing 0.9.5d)
breadboards: 1

parts:
  M3 = ESP32-C3-DevKitM-1 [part_number=ESP32-C3-DevKitM-1]
  M1 = Dagu DGServo 9g (Top view) [part_number=RS001B]
  C2 = Capacitor Polarized [package=nippon_f80]
  C3 = Capacitor Polarized [package=nippon_f80]
  C4 = Capacitor Polarized [package=nippon_f80]

nets:
  N1: M3.GND-16, M1.vcc, C2.+, C3.+, C4.+
  N2: M3.2, M1.pulse
  N3: M3.5V-28, M3.5V-29, M1.gnd, C2.-, C3.-, C4.-

custom parts:
  ESP32-C3-DevKitM-1: Espressif Esp32 DevKit v1 is one of the development board created by DOIT to evaluate the ESP-WROOM-32 module. It is based on the ESP32 microcontroller that boasts Wifi, Bluetooth, Ethernet and Low Power support all in a single chip. (vanepp) Feb 2021: converted to ESP32-C3-DevKitM-1. This chip is 30pins long (2 x15) and 11 pins width.
